# Fritzing sketch MCP2221A_SO1602A_I2C (saved by Fritzing 0.9.4)
breadboards: 2

parts:
  LCD1 = LCD screen
  S1 = Toggle Switch [package=THT]
  C1 = Ceramic Capacitor [capacitance=0.1µF voltage=16V package="100 mil [THT, multilayer]"]
  R1 = Resistor [tolerance=±5% resistance=4.7k package=THT]
  R2 = Resistor [tolerance=±5% resistance=4.7k package=THT]
  CONN1 = USB connector [package=THT]
  IC1 = IC, DIP package, 14 pins [chip_label=MCP2221A]
  C2 = Ceramic Capacitor [capacitance=0.22µF voltage=16V package="100 mil [THT, multilayer]"]
  C3 = Ceramic Capacitor [capacitance=0.1µF voltage=16V package="100 mil [THT, multilayer]"]
  REG_3_3V = Voltage Regulator - 3.3V [package="TO220 [THT]"]
  C4 = Ceramic Capacitor [capacitance=0.1µF voltage=16V package="100 mil [THT, multilayer]"]
  C5 = Electrolytic Capacitor [capacitance=47µF voltage=35V package="100 mil [THT, electrolytic]"]
  R3 = Resistor [tolerance=±5% resistance=10k package=THT]

nets:
  GND: LCD1.VSS, LCD1.V0, S1.L2, C1.1, CONN1.GND, CONN1.chassis5, CONN1.chassis6, IC1.pin14, C2.0, C3.0, REG_3_3V.GND, C4.1, C5.-
  N1: LCD1.VDD, S1.L1, C1.0, R1.Pin_0, R2.Pin_0, IC1.pin11, C2.1, REG_3_3V.output_voltage, C5.+
  N2: LCD1.RS, S1.COM
  N3: LCD1.DB0, R1.Pin_1, IC1.pin10
  N4: LCD1.DB1, LCD1.DB2, R2.Pin_1, IC1.pin9
  N5: CONN1.5V, IC1.pin1, REG_3_3V.input_voltage, C4.0, R3.Pin_0
  N6: CONN1.d-, IC1.pin12
  N7: CONN1.d+, IC1.pin13
  N8: IC1.pin4, C3.1, R3.Pin_1

notes:
  1:VSS
  4:SA0
  2:VDD
  8:SDAin
  7:SCL
  3:/CS
  9:SDAout
  0x3D
  0x3C
  SO2002A/SO2016A
  D-
  D+
  3.3V
  VBUS
  GND
  ←PC
  SCL
  SDA
