# Fritzing sketch RaspberryPi_SO1602A_I2C (saved by Fritzing 0.9.4)
breadboards: 1

parts:
  Raspberry_Pi_1 = Raspberry Pi 3 [part_number=RPI-3-V1.2]
  LCD1 = LCD screen
  S1 = Toggle Switch [package=THT]
  C1 = Ceramic Capacitor [capacitance=0.1µF voltage=16V package="100 mil [THT, multilayer]"]
  R1 = Resistor [tolerance=±5% resistance=4.7k package=THT]
  R2 = Resistor [tolerance=±5% resistance=4.7k package=THT]

nets:
  3V3: Raspberry_Pi_1.3v3, LCD1.VDD, S1.L1, C1.0, R1.Pin_0, R2.Pin_0
  N1: Raspberry_Pi_1.GPIO2, LCD1.DB1, LCD1.DB2, R2.Pin_1
  N2: Raspberry_Pi_1.GPIO3, LCD1.DB0, R1.Pin_1
  GND: Raspberry_Pi_1.GND, LCD1.VSS, LCD1.V0, S1.L2, C1.1
  N3: LCD1.RS, S1.COM

notes:
  1:VSS
  4:SA0
  2:VDD
  8:SDAin
  7:SCL
  3:/CS
  9:SDAout
  0x3D
  0x3C
  SO2002A/SO2016A
  SCL
  SDA
  GND
  3.3V
